# Fritzing sketch csarduino_diagram_v03 (saved by Fritzing 0.9.3b)

parts:
  Componente1 = Arduino Nano (Rev3.0)
  M1 = Stepper Motor - Bipolar
  hc-sr1 = hc-sr04
  Pololu_A1 = Pololu A4988 [package=SO16]
  J10 = male pin header, 3 pins [form="♂ (male)"]  # not connected
  J11 = male pin header, 3 pins [form="♂ (male)"]  # not connected
  J12 = male pin header, 3 pins [form="♂ (male)"]  # not connected
  J13 = male pin header, 3 pins [form="♂ (male)"]  # not connected
  J14 = male pin header, 3 pins [form="♂ (male)"]  # not connected
  J15 = male pin header, 3 pins [form="♂ (male)"]
  J16 = male pin header, 3 pins [form="♂ (male)"]  # not connected
  J17 = male pin header, 3 pins [form="♂ (male)"]
  J18 = male pin header, 3 pins [form="♂ (male)"]  # not connected
  J19 = male pin header, 3 pins [form="♂ (male)"]  # not connected
  U1 = LIPO-110mAh [package=lipo-110]
  hc-sr2 = hc-sr04
  U2 = LIPO-110mAh [package=lipo-110]

nets:
  N1: Componente1.D3, J17.pin1
  N2: Componente1.D5, hc-sr2.Echo
  N3: Componente1.D6, hc-sr2.Trig
  N4: Componente1.D7, Pololu_A1.DIR
  N5: Componente1.D8, Pololu_A1.STEP
  N6: Componente1.D9, Pololu_A1.ENABLE
  N7: Componente1.D10, hc-sr1.Echo
  N8: Componente1.D11/MOSI, hc-sr1.Trig
  N9: Componente1.VIN, U2.+
  N10: Componente1.GND, J15.pin3
  N11: Componente1.5V, J15.pin2
  N12: M1.A, Pololu_A1.2B
  N13: M1.C, Pololu_A1.2A
  N14: M1.B, Pololu_A1.1A
  N15: M1.D, Pololu_A1.1B
  N16: Pololu_A1.GND#14, U1.-
  N17: Pololu_A1.VMOT, U1.+

notes:
  S + -
